// Logisim project Resposta 3 pt3.circ as structural Verilog: 1 circuit, main circuit main
module main (
  input  A,
  input  B,
  input  C,
  input  D,
  output S
);

  wire nor_1_out, nor_2_out, nor_3_out, nor_4_out, nor_5_out, nor_6_out, nor_7_out, nor_8_out, nor_9_out,
       nor_10_out, nor_11_out, nor_12_out, nor_13_out, nor_14_out, nor_15_out, nor_16_out, nor_17_out;

  nor nor_1 (nor_1_out, D, D);
  nor nor_2 (nor_2_out, B, B);
  nor nor_3 (nor_3_out, C, C);
  nor nor_4 (nor_4_out, D, D);
  nor nor_5 (nor_5_out, A, A);
  nor nor_6 (nor_6_out, nor_4_out, nor_4_out);
  nor nor_7 (nor_7_out, nor_1_out, nor_2_out, nor_3_out);
  nor nor_8 (nor_8_out, B, A);
  nor nor_9 (nor_9_out, nor_7_out, nor_7_out);
  nor nor_10 (nor_10_out, nor_8_out, nor_8_out);
  nor nor_11 (nor_11_out, nor_5_out, nor_6_out);
  nor nor_12 (nor_12_out, nor_9_out, nor_10_out);
  nor nor_13 (nor_13_out, nor_11_out, nor_11_out);
  nor nor_14 (nor_14_out, nor_12_out, nor_12_out);
  nor nor_15 (nor_15_out, nor_13_out, nor_13_out);
  nor nor_16 (nor_16_out, nor_14_out, nor_14_out);
  nor nor_17 (nor_17_out, nor_16_out, nor_15_out);
  nor nor_18 (S, nor_17_out, nor_17_out);
endmodule
