// Logisim project 3 - Multiplexador com Flipflop.circ as structural Verilog: 1 circuit, main circuit main
module main (
  input  Clock,
  input  E,
  input  SEL,
  output out_4
);

  wire multiplexer_1_out;

  Multiplexer #(.enable("false")) multiplexer_1 (.in0(out_4), .in1(E), .out(multiplexer_1_out), .sel(SEL));
  D_Flip_Flop d_ff_1 (.clk(Clock), .D(multiplexer_1_out), .Q(out_4));  // open: Qn, preset, en, reset
endmodule
