// Logisim project Resposta 1.circ as structural Verilog: 1 circuit, main circuit main
module main (
  input  in_1,
  input  A,
  input  B,
  input  C,
  input  D,
  input  A_2,
  input  B_2,
  input  C_2,
  input  D_2,
  input  in_10,
  input  in_11,
  input  in_12,
  input  in_13,
  input  in_14,
  input  in_15,
  input  in_16,
  input  in_17,
  input  in_18,
  input  in_19,
  input  in_20,
  output out_21,
  output out_22,
  output S,
  output S_2,
  output out_25,
  output out_26
);

  wire and_2_out, and_4_out, nand_2_out, nand_3_out, nand_4_out, nor_2_out, nor_3_out, not_1_out, not_2_out,
       or_2_out, or_3_out;

  and and_1 (out_21, in_1, in_10, in_11);
  or or_1 (out_22, in_12, in_13, in_14);
  nand nand_1 (out_25, in_15, in_16, in_17);
  nor nor_1 (out_26, in_18, in_19, in_20);
  and and_2 (and_2_out, D, C);
  or or_2 (or_2_out, B, A);
  nor nor_2 (nor_2_out, C, B);
  not not_1 (not_1_out, D);
  or or_3 (or_3_out, nor_2_out, not_1_out);
  nand nand_2 (nand_2_out, and_2_out, or_2_out);
  and and_3 (S_2, nand_2_out, or_3_out);
  and and_4 (and_4_out, D_2, B_2, C_2);
  nor nor_3 (nor_3_out, B_2, A_2);
  not not_2 (not_2_out, D_2);
  nand nand_3 (nand_3_out, and_4_out, nor_3_out);
  nand nand_4 (nand_4_out, A_2, not_2_out);
  nand nand_5 (S, nand_3_out, nand_4_out);
endmodule
