// Logisim project Resposta 2 pt1.circ as structural Verilog: 1 circuit, main circuit main
module main (
  input  A,
  input  B,
  input  C,
  input  A_2,
  input  B_2,
  input  C_2,
  input  A_3,
  input  B_3,
  input  C_3,
  input  A_4,
  input  B_4,
  input  C_4,
  output S,
  output S_2,
  output S_3,
  output S_4
);

  wire nand_1_out, nand_2_out, nand_3_out, nand_4_out, nand_5_out, nand_6_out, nand_7_out, nand_10_out;

  nand nand_1 (nand_1_out, A_2, A_2);
  nand nand_2 (nand_2_out, B_2, B_2);
  nand nand_3 (nand_3_out, C_2, C_2);
  nand nand_4 (nand_4_out, A_4, A_4);
  nand nand_5 (nand_5_out, B_4, B_4);
  nand nand_6 (nand_6_out, C_4, C_4);
  nand nand_7 (nand_7_out, A, B, C);
  nand nand_8 (S_3, A_3, B_3, C_3);
  nand nand_9 (S_2, nand_1_out, nand_2_out, nand_3_out);
  nand nand_10 (nand_10_out, nand_4_out, nand_5_out, nand_6_out);
  nand nand_11 (S, nand_7_out, nand_7_out);
  nand nand_12 (S_4, nand_10_out, nand_10_out);

  // Notes on the sheet:
  //   porta and com nand
  //   porta or com nand
  //   porta nand com nand
  //   porta nor com nand
endmodule
