// Logisim project Resposta 3 pt1.circ as structural Verilog: 1 circuit, main circuit main
module main (
  input  A,
  input  A_2,
  input  B,
  input  B_2,
  input  C,
  input  C_2,
  input  A_3,
  input  A_4,
  input  B_3,
  input  B_4,
  input  C_3,
  input  C_4,
  output S,
  output S_2,
  output S_3,
  output S_4
);

  wire nor_1_out, nor_2_out, nor_3_out, nor_4_out, nor_7_out, nor_8_out, nor_9_out, nor_11_out;

  nor nor_1 (nor_1_out, A, A);
  nor nor_2 (nor_2_out, B, B);
  nor nor_3 (nor_3_out, C, C);
  nor nor_4 (nor_4_out, A_3, B_3, C_3);
  nor nor_5 (S, nor_1_out, nor_2_out, nor_3_out);
  nor nor_6 (S_4, nor_4_out, nor_4_out);
  nor nor_7 (nor_7_out, A_2, A_2);
  nor nor_8 (nor_8_out, B_2, B_2);
  nor nor_9 (nor_9_out, C_2, C_2);
  nor nor_10 (S_3, A_4, B_4, C_4);
  nor nor_11 (nor_11_out, nor_7_out, nor_8_out, nor_9_out);
  nor nor_12 (S_2, nor_11_out, nor_11_out);

  // Notes on the sheet:
  //   porta and com nor
  //   porta or com nor
  //   porta nand com nor
  //   porta nor com nor
endmodule
