// Logisim project Resposta 5.1.circ as structural Verilog: 1 circuit, main circuit main
module main (
  input  A,
  input  B,
  input  C,
  input  A_2,
  input  B_2,
  input  C_2,
  output S
);

  wire and_1_out, not_1_out, or_1_out;

  not not_1 (not_1_out, C);
  or or_1 (or_1_out, not_1_out, and_1_out);
  and and_1 (and_1_out, B, C);
  and and_2 (S, or_1_out, A);

  // Notes on the sheet:
  //   Resposta 5.1
  //   Resposta 5.2
endmodule
