// Logisim project 1 - Multiplexador.circ as structural Verilog: 2 circuits, main circuit main
module main (
  input  A,
  input  B,
  input  SEL,
  input  SEL_2,
  input  A_2,
  input  B_2,
  output \SAÍDA ,
  output out_8
);

  wire and_1_out, and_2_out, not_1_out;

  Multiplexer #(.enable("false")) multiplexer_1 (.in0(A), .in1(B), .out(\SAÍDA ), .sel(SEL));
  not not_1 (not_1_out, SEL_2);
  and and_1 (and_1_out, not_1_out, A_2);
  and and_2 (and_2_out, SEL_2, B_2);
  or or_1 (out_8, and_1_out, and_2_out);
endmodule

module flip_flop (
  input  D,
  input  Clock,
  input  SEL,
  input  A,
  input  B,
  output Q,
  output out_7
);

  wire and_1_out, and_2_out, and_3_out, and_4_out, nor_1_out, not_1_out, not_2_out;

  not not_1 (not_1_out, D);
  and and_1 (and_1_out, D, Clock);
  and and_2 (and_2_out, Clock, not_1_out);
  not not_2 (not_2_out, SEL);
  and and_3 (and_3_out, not_2_out, A);
  and and_4 (and_4_out, SEL, B);
  or or_1 (out_7, and_3_out, and_4_out);
  nor nor_1 (nor_1_out, and_1_out, Q);
  nor nor_2 (Q, nor_1_out, and_2_out);
endmodule
