// Logisim project 4 - Memoria 1 byte.circ as structural Verilog: 1 circuit, main circuit main
module main (
  input  [7:0] ENTRADA,
  input  Clock,
  input  SEL,
  output [7:0] SAIDA
);

  _3___Multiplexador_com_Flipflop_main main_1 (.Clock(Clock), .E(ENTRADA[7]), .SEL(SEL), .out_4(SAIDA[7]));
  _3___Multiplexador_com_Flipflop_main main_2 (.Clock(Clock), .E(ENTRADA[0]), .SEL(SEL), .out_4(SAIDA[0]));
  _3___Multiplexador_com_Flipflop_main main_3 (.Clock(Clock), .E(ENTRADA[6]), .SEL(SEL), .out_4(SAIDA[6]));
  _3___Multiplexador_com_Flipflop_main main_4 (.Clock(Clock), .E(ENTRADA[1]), .SEL(SEL), .out_4(SAIDA[1]));
  _3___Multiplexador_com_Flipflop_main main_5 (.Clock(Clock), .E(ENTRADA[5]), .SEL(SEL), .out_4(SAIDA[5]));
  _3___Multiplexador_com_Flipflop_main main_6 (.Clock(Clock), .E(ENTRADA[2]), .SEL(SEL), .out_4(SAIDA[2]));
  _3___Multiplexador_com_Flipflop_main main_7 (.Clock(Clock), .E(ENTRADA[4]), .SEL(SEL), .out_4(SAIDA[4]));
  _3___Multiplexador_com_Flipflop_main main_8 (.Clock(Clock), .E(ENTRADA[3]), .SEL(SEL), .out_4(SAIDA[3]));
endmodule
