// Logisim project MeioSomador.circ as structural Verilog: 1 circuit, main circuit main
module main (
  input  A,
  input  B,
  output R,
  output VAI1
);

  xor xor_1 (R, A, B);
  and and_1 (VAI1, A, B);
endmodule
