// Logisim project Somador2Bits.circ as structural Verilog: 1 circuit, main circuit main
module main (
  input  V1D1,
  input  V2D1,
  input  V1D2,
  input  V2D2,
  output out_5,
  output out_6,
  output out_7,
  output Carry_Out
);

  wire and_1_out, and_2_out, and_3_out, and_4_out, and_5_out, and_6_out, and_7_out, not_1_out, not_2_out,
       not_3_out, not_4_out, not_5_out, not_6_out;

  not not_1 (not_1_out, V1D1);
  not not_2 (not_2_out, V2D1);
  not not_3 (not_3_out, V1D1);
  not not_4 (not_4_out, Carry_Out);
  not not_5 (not_5_out, V2D1);
  not not_6 (not_6_out, Carry_Out);
  and and_1 (and_1_out, V2D1, V1D1);
  and and_2 (and_2_out, V2D1, Carry_Out);
  and and_3 (and_3_out, V1D1, Carry_Out);
  and and_4 (and_4_out, not_1_out, not_2_out, Carry_Out);
  and and_5 (and_5_out, not_3_out, V2D1, not_4_out);
  and and_6 (and_6_out, V1D1, not_5_out, not_6_out);
  and and_7 (and_7_out, V1D1, V2D1, Carry_Out);
  xor xor_1 (out_7, V1D2, V2D2);
  and and_8 (Carry_Out, V2D2, V1D2);
  or or_1 (out_5, and_1_out, and_2_out, and_3_out);
  or or_2 (out_6, and_4_out, and_5_out, and_6_out, and_7_out);
endmodule
