// Logisim project Somador4Bits.circ as structural Verilog: 1 circuit, main circuit main
module main (
  input  [3:0] in_1,
  input  [3:0] in_2,
  output out_3,
  output out_4,
  output out_5,
  output out_6,
  output out_7
);

  wire main_1_vai1, main_2_p5, main_3_p5;

  MeioSomador_main main_1 (.A(in_1[0]), .B(in_2[0]), .R(out_7), .VAI1(main_1_vai1));
  // Somador_main main_2: pin names not known; wires that end beside it: main_1_vai1, in_1[1], in_2[1], out_6, main_2_p5
  // Somador_main main_3: pin names not known; wires that end beside it: main_2_p5, in_1[2], in_2[2], out_5, main_3_p5
  // Somador_main main_4: pin names not known; wires that end beside it: main_3_p5, in_1[3], in_2[3], out_4, out_3

  // Notes on the sheet:
  //   Meio Somador
  //   Somador 1
  //   Somador 2
  //   Somador 3
endmodule
