// Logisim project SomadorCompleto.circ as structural Verilog: 1 circuit, main circuit main
module main (
  input  VEM1,
  input  A,
  input  B,
  output out_4,
  output VAI1
);

  wire and_1_out, and_2_out, and_3_out, xor_1_out;

  and and_1 (and_1_out, VEM1, A);
  and and_2 (and_2_out, VEM1, B);
  and and_3 (and_3_out, A, B);
  xor xor_1 (xor_1_out, VEM1, A);
  or or_1 (VAI1, and_1_out, and_2_out, and_3_out);
  xor xor_2 (out_4, xor_1_out, B);
endmodule
