// Logisim project Resposta 5.3.circ as structural Verilog: 1 circuit, main circuit main
module main (
  input  F,
  input  C,
  input  B,
  input  P,
  output Obturador,
  output Flash
);

  wire and_1_out, and_2_out, and_3_out, not_1_out, not_2_out, not_3_out, not_4_out, not_5_out, not_6_out,
       not_7_out;

  not not_1 (not_1_out, F);
  not not_2 (not_2_out, P);
  not not_3 (not_3_out, C);
  not not_4 (not_4_out, P);
  not not_5 (not_5_out, P);
  not not_6 (not_6_out, F);
  not not_7 (not_7_out, P);
  and and_1 (and_1_out, not_1_out, C, B, not_2_out);
  and and_2 (and_2_out, F, not_3_out, B, not_4_out);
  and and_3 (and_3_out, F, C, B, not_5_out);
  and and_4 (Flash, not_6_out, C, B, not_7_out);
  or or_1 (Obturador, and_1_out, and_2_out, and_3_out);
endmodule
