// Logisim project main.circ as structural Verilog: 1 circuit, main circuit main
module main (
  input  [7:0] A,
  input  [3:0] Clock_s,
  input  [7:0] B,
  input  SEL,
  input  [1:0] \Operação ,
  input  [1:0] \Memória ,
  output [7:0] Memoria_0,
  output [7:0] Memoria_1,
  output [7:0] Memoria_2,
  output [7:0] Memoria_3
);

  wire [7:0] adder_1_out, adder_2_out, and_1_out, demultiplexer_1_out0, demultiplexer_1_out1,
       demultiplexer_1_out2, demultiplexer_1_out3, multiplexer_1_out, not_1_out, or_1_out;

  assign not_1_out = ~B;  // NOT_Gate not_1, 8 bits wide
  assign and_1_out = A & B;  // AND_Gate and_1, 8 bits wide
  assign or_1_out = A | B;  // OR_Gate or_1, 8 bits wide
  Adder adder_1 (.a(A), .b(B), .out(adder_1_out), .cin(1'b0));  // open: cout
  Adder adder_2 (.a(A), .b(not_1_out), .out(adder_2_out), .cin(1'b1));  // open: cout
  Multiplexer #(.select(2), .width(8)) multiplexer_1 (
    .in0(and_1_out), .in1(or_1_out), .in2(adder_1_out), .in3(adder_2_out), .out(multiplexer_1_out),
    .sel(\Operação ), .en(1'b1));
  Demultiplexer #(.select(2), .width(8)) demultiplexer_1 (
    .out0(demultiplexer_1_out0), .out1(demultiplexer_1_out1), .out2(demultiplexer_1_out2),
    .out3(demultiplexer_1_out3), .in(multiplexer_1_out), .sel(\Memória ), .en(1'b1));
  _4___Memoria_1_byte_main main_1 (.SEL(SEL), .Clock(Clock_s[0]), .SAIDA(Memoria_0), .ENTRADA(demultiplexer_1_out0));
  _4___Memoria_1_byte_main main_2 (.SEL(SEL), .Clock(Clock_s[1]), .SAIDA(Memoria_1), .ENTRADA(demultiplexer_1_out1));
  _4___Memoria_1_byte_main main_3 (.SEL(SEL), .Clock(Clock_s[2]), .SAIDA(Memoria_2), .ENTRADA(demultiplexer_1_out2));
  _4___Memoria_1_byte_main main_4 (.SEL(SEL), .Clock(Clock_s[3]), .SAIDA(Memoria_3), .ENTRADA(demultiplexer_1_out3));
endmodule
